# Fritzing sketch circuit_diagram (saved by Fritzing 0.9.3b)
breadboards: 17
perfboards: 1

parts:
  U1 = IC, DIP package, 20 pins [chip_label=SN74LS682N]
  U2 = IC, DIP package, 20 pins [chip_label=SN74LS682N]
  U3 = IC, DIP package, 20 pins [chip_label=SN74LS244N]
  U4 = IC, DIP package, 20 pins [chip_label=SN74LS244N]
  U5 = IC, DIP package, 14 pins [chip_label=SN74LS74AN]
  U6 = IC, DIP package, 14 pins [chip_label=SN74HCT32N]
  U7 = IC, DIP package, 20 pins [chip_label=SN74LS682N]
  U8 = IC, DIP package, 20 pins [chip_label=SN74LS682N]
  U9 = IC, DIP package, 14 pins [chip_label=SN74HCT32N]
  U10 = IC, DIP package, 20 pins [chip_label=SN74LS245N]
  U11 = IC, DIP package, 20 pins [chip_label=SN74LS682N]
  U12 = IC, DIP package, 20 pins [chip_label=SN74LS682N]
  U13 = IC, DIP package, 20 pins [chip_label=SN74LS682N]
  U14 = IC, DIP package, 20 pins [chip_label=SN74LS682N]
  U15 = IC, DIP package, 20 pins [chip_label=SN74LS245N]
  U16 = IC, DIP package, 20 pins [chip_label=SN74LS244N]
  U17 = IC, DIP package, 14 pins [chip_label=SN74LS74AN]
  U18 = IC, DIP package, 20 pins [chip_label=SN74LS682N]
  U19 = IC, DIP package, 20 pins [chip_label=SN74LS682N]
  U20 = IC, DIP package, 16 pins [chip_label=SN74LS161A]
  U21 = IC, DIP package, 16 pins [chip_label=SN74LS161A]
  U22 = IC, DIP package, 14 pins [chip_label=SN74HCT32N]
  U23 = IC, DIP package, 16 pins [chip_label=SN74LS161A]
  U24 = IC, DIP package, 20 pins [chip_label=SN74LS244N]
  U25 = IC, DIP package, 16 pins [chip_label=SN74LS161A]
  U26 = IC, DIP package, 16 pins [chip_label=SN74LS161A]
  U27 = IC, DIP package, 20 pins [chip_label=SN74LS682N]
  U28 = IC, DIP package, 20 pins [chip_label=SN74LS682N]
  U29 = IC, DIP package, 20 pins [chip_label=SN74LS244N]
  U30 = IC, DIP package, 14 pins [chip_label=SN74HCT32N]
  U31 = IC, DIP package, 14 pins [chip_label=SN74LS74AN]
  U32 = IC, DIP package, 16 pins [chip_label=SN74LS161A]
  U33 = IC, DIP package, 16 pins [chip_label=SN74LS283N]
  U34 = IC, DIP package, 16 pins [chip_label=SN74LS283N]
  U35 = IC, DIP package, 16 pins [chip_label=SN74LS283N]
  U36 = IC, DIP package, 16 pins [chip_label=SN74LS283N]
  U37 = IC, DIP package, 20 pins [chip_label=SN74LS682N]
  U38 = IC, DIP package, 20 pins [chip_label=SN74LS682N]
  U39 = IC, DIP package, 20 pins [chip_label=SN74LS273N]
  U40 = IC, DIP package, 20 pins [chip_label=SN74LS273N]
  U43 = IC, DIP package, 20 pins [chip_label=SN74HCT374N]
  U44 = IC, DIP package, 20 pins [chip_label=SN74HCT374N]
  U45 = IC, DIP package, 14 pins [chip_label=SN74LS74AN]
  U46 = IC, DIP package, 14 pins [chip_label=SN74HCT32N]
  U47 = IC, DIP package, 20 pins [chip_label=SN74LS244N]
  U48 = IC, DIP package, 20 pins [chip_label=SN74LS245N]
  U49 = IC, DIP package, 20 pins [chip_label=SN74LS245N]
  U50 = IC, DIP package, 20 pins [chip_label=SN74LS245N]
  U51 = IC, DIP package, 20 pins [chip_label=SN74LS682N]
  U52 = IC, DIP package, 20 pins [chip_label=SN74LS682N]
  U53 = IC, DIP package, 14 pins [chip_label=SN74LS08N]
  U54 = IC, DIP package, 14 pins [chip_label=SN74LS04N]
  U55 = IC, DIP package, 14 pins [chip_label=SN74LS74AN]
  U56 = IC, DIP package, 28 pins [chip_label=CY7C199-55PC]
  U57 = IC, DIP package, 20 pins [chip_label=SN74LS244N]
  U58 = IC, DIP package, 20 pins [chip_label=SN74LS244N]
  U59 = IC, DIP package, 20 pins [chip_label=SN74LS244N]
  U60 = IC, DIP package, 20 pins [chip_label=SN74LS244N]
  U61 = IC, DIP package, 20 pins [chip_label=SN74LS244N]
  U62 = IC, DIP package, 20 pins [chip_label=SN74LS273N]
  U63 = IC, DIP package, 16 pins [chip_label=SN74LS161A]
  U64 = IC, DIP package, 16 pins [chip_label=SN74LS161A]
  U65 = IC, DIP package, 20 pins [chip_label=SN74LS273N]
  U66 = IC, DIP package, 16 pins [chip_label=SN74LS283N]
  U67 = IC, DIP package, 16 pins [chip_label=SN74LS283N]
  U68 = IC, DIP package, 16 pins [chip_label=SN74LS283N]
  U69 = IC, DIP package, 16 pins [chip_label=SN74LS283N]
  U70 = IC, DIP package, 20 pins [chip_label=SN74LS273N]
  U71 = IC, DIP package, 20 pins [chip_label=SN74LS273N]
  U72 = IC, DIP package, 20 pins [chip_label=SN74LS273N]
  U73 = IC, DIP package, 20 pins [chip_label=SN74LS273N]  # not connected
  U74 = IC, DIP package, 20 pins [chip_label=SN74LS273N]  # not connected
  U75 = IC, DIP package, 14 pins [chip_label=SN74LS04N]  # not connected
  U76 = IC, DIP package, 20 pins [chip_label=SN74LS244N]
  U77 = IC, DIP package, 20 pins [chip_label=SN74LS682N]
  U78 = IC, DIP package, 20 pins [chip_label=SN74LS682N]
  U79 = IC, DIP package, 20 pins [chip_label=SN74LS682N]
  U80 = IC, DIP package, 14 pins [chip_label=SN74HCT32N]
  U81 = IC, DIP package, 14 pins [chip_label=SN74HCT32N]
  U82 = IC, DIP package, 14 pins [chip_label=SN74LS04N]
  U83 = IC, DIP package, 20 pins [chip_label=SN74LS682N]
  R1 = Resistor [tolerance=±5% resistance=2.2k package=THT]
  R2 = Resistor [tolerance=±5% resistance=2.2k package=THT]
  R3 = Resistor [tolerance=±5% resistance=2.2k package=THT]
  R4 = Resistor [tolerance=±5% resistance=2.2k package=THT]
  R5 = Resistor [tolerance=±5% resistance=2.2k package=THT]
  R6 = Resistor [tolerance=±5% resistance=2.2k package=THT]
  R7 = Resistor [tolerance=±5% resistance=2.2k package=THT]
  R8 = Resistor [tolerance=±5% resistance=2.2k package=THT]
  R9 = Resistor [tolerance=±5% resistance=2.2k package=THT]
  R10 = Resistor [tolerance=±5% resistance=357 package=THT]
  R11 = Resistor [tolerance=±5% resistance=357 package=THT]
  R12 = Resistor [tolerance=±5% resistance=357 package=THT]
  R13 = Resistor [tolerance=±5% resistance=100 package=THT]
  R14 = Resistor [tolerance=±5% resistance=100 package=THT]
  R15 = Resistor [tolerance=±5% resistance=100 package=THT]
  R16 = Resistor [tolerance=±5% resistance=220 package=THT]
  XTAL1 = Crystal [frequency="25 MHz" package=SMD]  # not connected

nets:
  N1: U1.pin2, U18.pin1
  N2: U1.pin3, U1.pin5, U1.pin7, U1.pin14, U1.pin18, U2.pin18, U2.pin20, U3.pin2, U3.pin17, U3.pin20, U4.pin2, U4.pin20, U5.pin10, U5.pin13, U5.pin14, U6.pin14, U7.pin14, U7.pin16, U7.pin20, U8.pin14, U8.pin20, U9.pin14, U10.pin1, U10.pin9, U10.pin20, U11.pin3, U11.pin5, U11.pin20, U12.pin20, U13.pin12, U13.pin14, U13.pin20, U14.pin7, U14.pin20, U15.pin20, U16.pin20, U17.pin1, U17.pin4, U17.pin14, U18.pin20, U19.pin3, U19.pin5, U19.pin14, U19.pin16, U19.pin18, U19.pin20, U20.pin9, U20.pin10, U20.pin16, U21.pin9, U21.pin16, U22.pin14, U23.pin9, U23.pin16, U24.pin2, U24.pin11, U24.pin20, U25.pin9, U25.pin10, U25.pin16, U26.pin9, U26.pin16, U27.pin20, U28.pin9, U28.pin12, U28.pin20, U29.pin13, U29.pin20, U30.pin14, U31.pin1, U31.pin4, U31.pin14, U32.pin7, U32.pin9, U32.pin10, U32.pin16, U33.pin16, U34.pin2, U34.pin11, U34.pin13, U34.pin16, U35.pin16, U36.pin16, U37.pin14, U37.pin20, U38.pin3, U38.pin7, U38.pin20, U39.pin20, U40.pin20, U43.pin20, U44.pin20, U45.pin1, U45.pin4, U45.pin14, U46.pin14, U47.pin20, U48.pin18, U48.pin20, U49.pin20, U50.pin20, U51.pin7, U51.pin14, U51.pin20, U52.pin3, U52.pin5, U52.pin14, U52.pin20, U53.pin14, U54.pin14, U55.pin10, U55.pin13, U55.pin14, U56.pin28, U57.pin20, U58.pin20, U59.pin20, U60.pin20, U61.pin13, U61.pin20, U62.pin1, U62.pin20, U63.pin7, U63.pin9, U63.pin10, U63.pin16, U64.pin9, U64.pin16, U65.pin1, U65.pin20, U66.pin16, U67.pin16, U68.pin16, U69.pin16, U70.pin1, U70.pin20, U71.pin1, U71.pin20, U72.pin1, U72.pin20, U76.pin11, U76.pin20, U77.pin3, U77.pin5, U77.pin6, U77.pin7, U77.pin8, U77.pin20, U78.pin5, U78.pin7, U78.pin20, U79.pin3, U79.pin7, U79.pin20, U80.pin14, U81.pin14, U82.pin14, U83.pin20, R1.Pin_1, R2.Pin_0, R5.Pin_1, R6.Pin_0, R9.Pin_0
  N3: U1.pin4, U8.pin11, U14.pin11, U18.pin2, U21.pin11
  N4: U1.pin6, U8.pin13, U14.pin13, U18.pin4, U21.pin12
  N5: U1.pin8, U8.pin15, U14.pin15, U18.pin6, U21.pin13
  N6: U1.pin9, U1.pin10, U1.pin12, U1.pin16, U1.pin20, U2.pin2, U2.pin3, U2.pin4, U2.pin5, U2.pin6, U2.pin7, U2.pin8, U2.pin9, U2.pin10, U2.pin12, U2.pin14, U2.pin16, U3.pin10, U4.pin4, U4.pin15, U4.pin17, U7.pin2, U7.pin3, U7.pin4, U7.pin5, U7.pin6, U7.pin7, U7.pin8, U7.pin9, U7.pin10, U7.pin12, U7.pin18, U8.pin3, U8.pin5, U8.pin7, U8.pin9, U8.pin10, U8.pin12, U8.pin16, U8.pin18, U9.pin7, U10.pin8, U10.pin10, U11.pin7, U11.pin9, U11.pin10, U11.pin12, U11.pin14, U11.pin16, U11.pin18, U12.pin2, U12.pin3, U12.pin4, U12.pin5, U12.pin6, U12.pin7, U12.pin8, U12.pin9, U12.pin10, U12.pin12, U12.pin14, U12.pin16, U12.pin18, U13.pin2, U13.pin3, U13.pin4, U13.pin5, U13.pin6, U13.pin7, U13.pin8, U13.pin9, U13.pin10, U13.pin16, U13.pin18, U14.pin3, U14.pin5, U14.pin9, U14.pin10, U14.pin12, U14.pin14, U14.pin16, U14.pin18, U15.pin10, U15.pin11, U15.pin12, U16.pin10, U17.pin7, U18.pin3, U18.pin5, U18.pin7, U18.pin9, U18.pin10, U18.pin12, U18.pin14, U18.pin16, U18.pin18, U19.pin7, U19.pin9, U19.pin10, U19.pin12, U20.pin8, U21.pin8, U22.pin7, U23.pin8, U24.pin10, U25.pin8, U26.pin8, U27.pin3, U27.pin5, U27.pin7, U27.pin9, U27.pin10, U27.pin12, U27.pin14, U27.pin16, U27.pin18, U28.pin3, U28.pin5, U28.pin7, U28.pin10, U28.pin14, U28.pin16, U28.pin18, U29.pin2, U29.pin4, U29.pin10, U29.pin11, U30.pin7, U31.pin7, U32.pin8, U33.pin2, U33.pin6, U33.pin7, U33.pin8, U33.pin11, U33.pin15, U34.pin6, U34.pin8, U34.pin15, U35.pin2, U35.pin6, U35.pin8, U35.pin11, U35.pin15, U36.pin2, U36.pin6, U36.pin8, U36.pin11, U36.pin15, U37.pin2, U37.pin3, U37.pin4, U37.pin5, U37.pin6, U37.pin7, U37.pin8, U37.pin9, U37.pin10, U37.pin12, U37.pin16, U37.pin18, U38.pin5, U38.pin9, U38.pin10, U38.pin12, U38.pin14, U38.pin16, U38.pin18, U39.pin10, U40.pin10, U43.pin10, U44.pin10, U45.pin7, U46.pin7, U47.pin10, U47.pin13, U47.pin15, U47.pin17, U48.pin10, U49.pin1, U49.pin10, U49.pin17, U49.pin18, U50.pin1, U50.pin10, U50.pin17, U50.pin18, U51.pin3, U51.pin5, U51.pin9, U51.pin10, U51.pin12, U51.pin16, U51.pin18, U52.pin7, U52.pin9, U52.pin10, U52.pin12, U52.pin16, U52.pin18, U53.pin7, U54.pin7, U55.pin7, U56.pin14, U56.pin22, U57.pin10, U58.pin10, U59.pin10, U60.pin10, U61.pin8, U61.pin10, U61.pin11, U62.pin10, U63.pin8, U64.pin8, U65.pin10, U66.pin3, U66.pin5, U66.pin7, U66.pin8, U66.pin9, U66.pin12, U66.pin14, U67.pin5, U67.pin7, U67.pin8, U68.pin8, U69.pin8, U70.pin10, U71.pin10, U72.pin10, U76.pin10, U77.pin4, U77.pin9, U77.pin10, U77.pin12, U77.pin14, U77.pin16, U77.pin18, U78.pin3, U78.pin9, U78.pin10, U78.pin12, U78.pin14, U78.pin16, U78.pin18, U79.pin5, U79.pin9, U79.pin10, U79.pin12, U79.pin14, U79.pin16, U79.pin18, U80.pin7, U81.pin7, U82.pin7, U83.pin3, U83.pin5, U83.pin7, U83.pin9, U83.pin10, U83.pin12, U83.pin14, U83.pin16, U83.pin18, R3.Pin_0, R4.Pin_1, R7.Pin_1, R8.Pin_1, R15.Pin_0, R16.Pin_1
  N7: U1.pin11, U7.pin11, U13.pin11, U18.pin11, U20.pin11
  N8: U1.pin13, U7.pin13, U13.pin13, U18.pin13, U20.pin12
  N9: U1.pin15, U7.pin15, U13.pin15, U18.pin15, U20.pin13
  N10: U1.pin17, U7.pin17, U13.pin17, U18.pin17, U20.pin14
  N11: U1.pin19, U6.pin1
  N12: U2.pin11, U8.pin2, U12.pin17, U14.pin2, U23.pin14
  N13: U2.pin13, U8.pin4, U12.pin15, U14.pin4, U23.pin13
  N14: U2.pin15, U8.pin6, U12.pin13, U14.pin6, U23.pin12
  N15: U2.pin17, U8.pin8, U12.pin11, U14.pin8, U23.pin11
  N16: U2.pin19, U6.pin2
  N17: U3.pin1, U4.pin5, R1.Pin_0
  N18: U3.pin3, U3.pin18, U5.pin11, R3.Pin_1
  N19: U3.pin19, U4.pin16, R2.Pin_1
  N20: U4.pin1, U6.pin6
  N21: U4.pin3, U4.pin18, U5.pin12
  N22: U4.pin19, U6.pin8
  N23: U5.pin9, U30.pin12
  N24: U6.pin3, U6.pin4
  N25: U6.pin5, U6.pin9, U22.pin12, U25.pin1, U25.pin2, U26.pin1, U26.pin2, U30.pin2, U30.pin5, U54.pin9, U55.pin9, U57.pin19, U58.pin19, U59.pin19, U60.pin19, U61.pin19, U63.pin2, U64.pin2
  N26: U6.pin10, U6.pin11
  N27: U6.pin12, U9.pin5, U12.pin19
  N28: U6.pin13, U9.pin4, U18.pin19
  N29: U7.pin19, U9.pin13
  N30: U8.pin17, U14.pin17, U18.pin8, U21.pin14
  N31: U8.pin19, U9.pin12
  N32: U9.pin6, U35.pin5, U39.pin1, U40.pin1, U53.pin4, U68.pin5
  N33: U9.pin11, U10.pin19
  N34: U10.pin11, U15.pin8, U17.pin2
  N35: U10.pin12, U15.pin9, U16.pin1
  N36: U11.pin2, U19.pin2, U26.pin11, U27.pin2, U28.pin2, U38.pin2, U51.pin2, U52.pin2
  N37: U11.pin4, U19.pin4, U26.pin12, U27.pin4, U28.pin4, U38.pin4, U51.pin4, U52.pin4
  N38: U11.pin6, U19.pin6, U26.pin13, U27.pin6, U28.pin6, U38.pin6, U51.pin6, U52.pin6
  N39: U11.pin8, U19.pin8, U26.pin14, U27.pin8, U28.pin8, U38.pin8, U51.pin8, U52.pin8
  N40: U11.pin11, U19.pin11, U25.pin11, U27.pin11, U28.pin11, U38.pin11, U51.pin11, U52.pin11
  N41: U11.pin13, U19.pin13, U25.pin12, U27.pin13, U28.pin13, U38.pin13, U51.pin13, U52.pin13
  N42: U11.pin15, U19.pin15, U25.pin13, U27.pin15, U28.pin15, U38.pin15, U51.pin15, U52.pin15
  N43: U11.pin17, U19.pin17, U25.pin14, U27.pin17, U28.pin17, U38.pin17, U51.pin17, U52.pin17
  N44: U11.pin19, U46.pin4
  N45: U13.pin19, U22.pin4
  N46: U14.pin19, U22.pin5
  N47: U15.pin19, U20.pin1, U21.pin1, U22.pin3, U23.pin1
  N48: U16.pin17, U17.pin3, R4.Pin_0
  N49: U19.pin19, U22.pin13
  N50: U20.pin2, U21.pin2, U22.pin1, U22.pin11, U23.pin2
  N51: U20.pin15, U21.pin7, U21.pin10
  N52: U21.pin15, U23.pin7, U23.pin10
  N53: U22.pin2, U22.pin6
  N54: U24.pin1, U29.pin18, R5.Pin_0
  N55: U24.pin9, U24.pin18, U31.pin3, R7.Pin_0
  N56: U24.pin19, U29.pin9, R6.Pin_1
  N57: U25.pin15, U26.pin7, U26.pin10
  N58: U27.pin19, U30.pin1
  N59: U28.pin19, U30.pin4
  N60: U29.pin1, U30.pin3
  N61: U29.pin7, U29.pin16, U31.pin2
  N62: U29.pin19, U30.pin6
  N63: U30.pin11, U47.pin1, U54.pin1
  N64: U30.pin13, U45.pin5
  N65: U31.pin5, U32.pin2
  N66: U32.pin1, U53.pin6
  N67: U32.pin11, U37.pin17
  N68: U32.pin13, U37.pin13, U37.pin15
  N69: U32.pin14, U37.pin11
  N70: U33.pin1, U43.pin3
  N71: U33.pin3, U39.pin5
  N72: U33.pin4, U39.pin3, U43.pin2
  N73: U33.pin5, U39.pin2
  N74: U33.pin9, U34.pin7
  N75: U33.pin10, U43.pin7
  N76: U33.pin12, U39.pin9
  N77: U33.pin13, U39.pin7, U43.pin6
  N78: U33.pin14, U39.pin6
  N79: U34.pin1, U43.pin14
  N80: U34.pin3, U39.pin15, U67.pin3
  N81: U34.pin4, U43.pin13
  N82: U34.pin5, U39.pin11, U46.pin8, U53.pin5
  N83: U34.pin9, U35.pin7
  N84: U34.pin10, U43.pin18
  N85: U34.pin12, U39.pin19, U43.pin17, U67.pin12
  N86: U34.pin14, U39.pin16, U67.pin14
  N87: U35.pin1, U44.pin3
  N88: U35.pin3, U40.pin5, U68.pin14
  N89: U35.pin4, U44.pin2
  N90: U35.pin9, U36.pin7
  N91: U35.pin10, U44.pin8
  N92: U35.pin12, U40.pin9, U68.pin12
  N93: U35.pin13, U44.pin7
  N94: U35.pin14, U40.pin4, U68.pin3
  N95: U36.pin1, U44.pin14
  N96: U36.pin3, U40.pin15, U69.pin3
  N97: U36.pin4, U44.pin13
  N98: U36.pin5, U40.pin12, U69.pin5
  N99: U36.pin10, U44.pin18
  N100: U36.pin12, U40.pin19, U69.pin12
  N101: U36.pin13, U44.pin17
  N102: U36.pin14, U40.pin16, U69.pin14
  N103: U37.pin19, U46.pin1, U46.pin5
  N104: U38.pin19, U46.pin2
  N105: U39.pin4, U43.pin5
  N106: U39.pin8, U43.pin9
  N107: U39.pin13, U43.pin12
  N108: U39.pin14, U43.pin15
  N109: U39.pin17, U43.pin16
  N110: U39.pin18, U43.pin19
  N111: U40.pin2, U44.pin1
  N112: U40.pin3, U44.pin4
  N113: U40.pin6, U44.pin5
  N114: U40.pin8, U44.pin9
  N115: U43.pin11, U44.pin11, U46.pin11
  N116: U45.pin2, U49.pin2, U50.pin2
  N117: U45.pin3, U48.pin1, R8.Pin_0
  N118: U46.pin3, U46.pin12
  N119: U46.pin6, U46.pin9
  N120: U46.pin10, U46.pin13
  N121: U47.pin2, U60.pin9
  N122: U47.pin3, U47.pin18, R10.Pin_1
  N123: U47.pin4, U61.pin3
  N124: U47.pin5, U47.pin16, R11.Pin_1
  N125: U47.pin6, U61.pin5
  N126: U47.pin7, U47.pin14, R12.Pin_1
  N127: U47.pin19, U54.pin2
  N128: U48.pin19, U49.pin3, U50.pin3, R9.Pin_1
  N129: U49.pin19, U52.pin19
  N130: U50.pin19, U51.pin19, U63.pin1, U64.pin1
  N131: U54.pin8, U62.pin11, U65.pin11
  N132: U55.pin8, U57.pin1, U58.pin1, U59.pin1, U60.pin1, U61.pin1
  N133: U55.pin11, U76.pin9, R16.Pin_0
  N134: U55.pin12, U70.pin3, U71.pin3, U72.pin3
  N135: U56.pin1, U58.pin5, U58.pin16
  N136: U56.pin2, U58.pin7, U58.pin14
  N137: U56.pin3, U58.pin9, U58.pin12
  N138: U56.pin4, U59.pin3, U59.pin18
  N139: U56.pin5, U59.pin5, U59.pin16
  N140: U56.pin6, U59.pin7, U59.pin14
  N141: U56.pin7, U59.pin9, U59.pin12
  N142: U56.pin8, U60.pin3, U60.pin18
  N143: U56.pin9, U60.pin5, U60.pin16
  N144: U56.pin10, U60.pin7, U60.pin14
  N145: U56.pin11, U60.pin12, U62.pin18
  N146: U56.pin12, U61.pin18, U62.pin17
  N147: U56.pin13, U61.pin16, U62.pin14
  N148: U56.pin20, U61.pin9, U61.pin12
  N149: U56.pin21, U57.pin3, U57.pin18
  N150: U56.pin23, U57.pin5, U57.pin16
  N151: U56.pin24, U57.pin7, U57.pin14
  N152: U56.pin25, U57.pin9, U57.pin12
  N153: U56.pin26, U58.pin3, U58.pin18
  N154: U56.pin27, U61.pin7, U61.pin14
  N155: U57.pin2, U70.pin2
  N156: U57.pin4, U70.pin5
  N157: U57.pin6, U70.pin6
  N158: U57.pin8, U70.pin9
  N159: U57.pin11, U66.pin10
  N160: U57.pin13, U66.pin13
  N161: U57.pin15, U66.pin1
  N162: U57.pin17, U66.pin4
  N163: U58.pin2, U70.pin12
  N164: U58.pin4, U70.pin15
  N165: U58.pin6, U70.pin16
  N166: U58.pin8, U70.pin19
  N167: U58.pin11, U67.pin10
  N168: U58.pin13, U67.pin13
  N169: U58.pin15, U67.pin1
  N170: U58.pin17, U67.pin4
  N171: U59.pin2, U71.pin2
  N172: U59.pin4, U71.pin5
  N173: U59.pin6, U71.pin6
  N174: U59.pin8, U71.pin9
  N175: U59.pin11, U68.pin10
  N176: U59.pin13, U68.pin13
  N177: U59.pin15, U68.pin2
  N178: U59.pin17, U68.pin4
  N179: U60.pin2, U71.pin12
  N180: U60.pin4, U71.pin15
  N181: U60.pin6, U71.pin16
  N182: U60.pin8, U72.pin2
  N183: U60.pin13, U69.pin13
  N184: U60.pin15, U69.pin2
  N185: U60.pin17, U69.pin4
  N186: U61.pin2, U72.pin5
  N187: U61.pin4, U72.pin6
  N188: U61.pin6, U81.pin6
  N189: U61.pin15, U62.pin15
  N190: U61.pin17, U62.pin16, U62.pin19
  N191: U63.pin11, U65.pin8
  N192: U63.pin12, U65.pin7
  N193: U63.pin13, U65.pin4
  N194: U63.pin14, U65.pin3
  N195: U63.pin15, U64.pin7, U64.pin10
  N196: U64.pin11, U65.pin18
  N197: U64.pin12, U65.pin17
  N198: U64.pin13, U65.pin14
  N199: U64.pin14, U65.pin13
  N200: U65.pin2, U66.pin6
  N201: U65.pin5, U66.pin2
  N202: U65.pin6, U66.pin15
  N203: U65.pin9, U66.pin11
  N204: U65.pin12, U67.pin6
  N205: U65.pin15, U67.pin2
  N206: U65.pin16, U67.pin15
  N207: U65.pin19, U67.pin11
  N208: U67.pin9, U68.pin7
  N209: U68.pin9, U69.pin7
  N210: U70.pin4, U71.pin4, U72.pin4
  N211: U70.pin7, U71.pin7, U72.pin7
  N212: U70.pin8, U71.pin8, U72.pin8
  N213: U70.pin11, U82.pin10
  N214: U70.pin13, U71.pin13, U72.pin13
  N215: U70.pin14, U71.pin14, U72.pin14
  N216: U70.pin17, U71.pin17, U72.pin17
  N217: U70.pin18, U71.pin18, U72.pin18
  N218: U71.pin11, U82.pin12
  N219: U72.pin11, U82.pin8
  N220: U76.pin19, U81.pin8
  N221: U77.pin2, U78.pin1
  N222: U77.pin11, U78.pin11, U79.pin11
  N223: U77.pin13, U78.pin13, U79.pin13
  N224: U77.pin15, U78.pin15, U79.pin15
  N225: U77.pin17, U78.pin17, U79.pin17
  N226: U77.pin19, U80.pin13
  N227: U78.pin2, U79.pin2
  N228: U78.pin4, U79.pin4
  N229: U78.pin6, U79.pin6
  N230: U78.pin8, U79.pin8
  N231: U78.pin19, U80.pin10
  N232: U79.pin19, U81.pin13
  N233: U80.pin1, U83.pin19
  N234: U80.pin3, U80.pin9, U80.pin12, U81.pin5, U81.pin9, U81.pin12
  N235: U80.pin8, U82.pin11
  N236: U80.pin11, U82.pin13
  N237: U81.pin11, U82.pin9
  N238: R10.Pin_0, R13.Pin_1
  N239: R11.Pin_0, R14.Pin_1
  N240: R12.Pin_0, R15.Pin_1

notes:
  5V DC
  Vertical Blanking
  To Vertical Sync
  To Horizontal Sync
  <- Horizontal Blanking
  To To To
  Red Green Blue
  32KB SRAM
  Switch between:
  Display Output mode (Q low).
  VRAM Program mode (Q high).
  Pixel offset counter |
  v
  Pixel offset + row starting address |
  v
  Row start address + 160 ^
  |
  Vectron 64 interface
  0 1 2 3
  Vectron 64 Data Bus
  Vectron 64 Data Bus
  4
  5
  6
  7
  Vectron 64 Address Bus
  7
  6
  5
  4
  3
  2
  1
  0
  Output of Vectron 64
  lower address bus comparator - $F8
  Output of Vectron 64 lower address comparator - $F9
  6502 Phase 1 Out
  Vectron 64 Address Bus
  15
  14
  13
  12
  11
  10
  9
  8
  25.175 MHz crystal oscillator divided by 4 = 6.29375 MHz output
